# Fritzing sketch Music_Display (saved by Fritzing 0.9.3b)

parts:
  Part1 = Arduino Uno (Rev3)
  Part2 = Bluetooth HM-10
  Part3 = OLED Monochrome 128x64 1.3 inch [part_number=938]

nets:
  N1: Part1.A4/SDA, Part3.MOSI_SDA
  N2: Part1.A5/SCL, Part3.SCLK_SCK
  N3: Part1.D0/RX, Part2.TXD
  N4: Part1.D1/TX, Part2.RXD
  N5: Part1.D4, Part3.RESET
  5V: Part1.5V, Part2.VCC, Part3.VIN
  GND: Part1.GND, Part2.GND, Part3.GND

custom parts:
  OLED Monochrome 128x64 1.3 inch: These displays are small, only about 1.3" diagonal, but very readable due to the high contrast of an OLED display. This display is made of 128x64 individual white OLED pixels, each one is turned on or off by the controller chip. Because the display makes its own light, no backlight is required. This reduces the power required to run the OLED and is why the display has such high contrast; we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
